// Logisim project bfcpu.circ as structural Verilog: 4 circuits, main circuit main
module main (
);

  wire and_1_out, button_1_out, controller_1_fdec, controller_1_halted, controller_1_rclk, controller_1_wclk,
       demultiplexer_1_out0, demultiplexer_1_out1, demultiplexer_1_out2, demultiplexer_1_out3, not_1_out,
       or_1_out;
  wire [1:0] controller_1_cycle, controller_1_seloperand;
  wire [3:0] rom_1_data;
  wire [6:0] keyboard_1_data;
  wire [7:0] BUF_q, BUF_q_2, controlled_buffer_1_out, controlled_buffer_2_out, controller_1_counter;
  wire [15:0] alu_1_x_prime, DP_q, multiplexer_1_out, PC_q;

  Button button_1 (.out(button_1_out));
  Keyboard #(.buflen(32), .trigger("rising")) keyboard_1 (
    .clk(button_1_out), .data(keyboard_1_data));  // open: re, clr, avail
  Register #(.width(16), .trigger("rising")) PC (
    .D({BUF_q_2, BUF_q}), .Q(PC_q), .clk(demultiplexer_1_out1));  // open: en, clr
  // Probe on {{9{1'b0}}, keyboard_1_data}
  ROM #(.addrWidth(16), .dataWidth(4)) rom_1 (.addr(PC_q), .data(rom_1_data));  // open: sel
  Demultiplexer #(.select(2), .width(1), .tristate("false")) demultiplexer_1 (
    .out0(demultiplexer_1_out0), .out1(demultiplexer_1_out1), .out2(demultiplexer_1_out2),
    .out3(demultiplexer_1_out3), .in(controller_1_wclk), .sel(controller_1_seloperand));
  // Probe on rom_1_data
  // Probe on button_1_out
  or or_1 (or_1_out, demultiplexer_1_out0, demultiplexer_1_out3);
  // Probe on controller_1_rclk
  // Probe on controller_1_wclk
  Controller controller_1 (
    .Opcode(rom_1_data), .Halt(button_1_out), .WCLK(controller_1_wclk), .RCLK(controller_1_rclk),
    .Halted(controller_1_halted), .Counter(controller_1_counter), .Cycle(controller_1_cycle),
    .selOperand(controller_1_seloperand), .fDec(controller_1_fdec));
  // Probe on controller_1_cycle
  // Probe on controller_1_counter
  LED #(.active("true")) Halted (.in(controller_1_halted));
  Register #(.width(16), .trigger("rising")) DP (
    .D({BUF_q_2, BUF_q}), .Q(DP_q), .clk(demultiplexer_1_out2));  // open: en, clr
  // Probe on controller_1_seloperand
  and and_1 (and_1_out, or_1_out, controller_1_wclk);
  not not_1 (not_1_out, and_1_out);
  // Probe on multiplexer_1_out
  Multiplexer #(.select(2), .width(16)) multiplexer_1 (
    .in0({{9{1'b0}}, keyboard_1_data}), .in1(PC_q), .in2(DP_q), .in3({{8{1'b0}}, controlled_buffer_2_out}),
    .out(multiplexer_1_out), .sel(controller_1_seloperand));
  // Probe on controller_1_fdec
  assign controlled_buffer_1_out = and_1_out ? BUF_q : 8'bz;  // Controlled_Buffer controlled_buffer_1
  RAM #(.addrWidth(16), .dataWidth(8), .bus("asynch")) ram_1 (
    .addr(DP_q), .data(controlled_buffer_1_out), .ld(not_1_out));  // open: sel, clr
  assign controlled_buffer_2_out = not_1_out ? controlled_buffer_1_out : 8'bz;  // Controlled_Buffer controlled_buffer_2
  // Probe on controlled_buffer_2_out
  // Probe on alu_1_x_prime
  ALU alu_1 (.x(multiplexer_1_out), .m(controller_1_fdec), .x_prime(alu_1_x_prime));
  // Probe on {BUF_q_2, BUF_q}
  Register #(.width(16), .trigger("rising")) BUF (
    .D(alu_1_x_prime), .Q({BUF_q_2, BUF_q}), .clk(controller_1_rclk));  // open: en, clr

  // Notes on the sheet:
  //   INPUT DRIVER
  //   PROGRAM ROM
  //   contents of rom_1 (hex, n*v repeats v):
  //   0 2 0 2
  //   CONTROL UNIT
  //   DATA RAM
  //   FIXME: Race condition when entering cycle 3
  //   srcMUX control vs. BUF clock
endmodule

module ALU (
  input  [15:0] x,
  input  m,
  output [15:0] x_prime
);

  wire adder_1_cout, adder_2_cout, adder_3_cout;

  Adder #(.width(4)) adder_1 (.a(x[3:0]), .b({{3{m}}, 1'b1}), .out(x_prime[3:0]), .cin(1'b0), .cout(adder_1_cout));
  Adder #(.width(4)) adder_2 (.a(x[7:4]), .b({4{m}}), .out(x_prime[7:4]), .cin(adder_1_cout), .cout(adder_2_cout));
  Adder #(.width(4)) adder_3 (.a(x[11:8]), .b({4{m}}), .out(x_prime[11:8]), .cin(adder_2_cout), .cout(adder_3_cout));
  Adder #(.width(4)) adder_4 (.a(x[15:12]), .b({4{m}}), .out(x_prime[15:12]), .cin(adder_3_cout));  // open: cout
endmodule

module xx (
  input  [7:0] D,
  input  en,
  input  clk,
  output [7:0] Q
);

  wire [7:0] multiplexer_1_out;

  Register #(.width(8), .trigger("rising")) register_1 (.D(multiplexer_1_out), .Q(Q), .clk(clk));  // open: en, clr
  Multiplexer #(.select(1), .width(8)) multiplexer_1 (.in0(Q), .in1(D), .out(multiplexer_1_out), .sel(en));
endmodule

module Controller (
  input  [3:0] Opcode,
  input  Halt,
  output WCLK,
  output RCLK,
  output [1:0] selOperand,
  output fDec,
  output Halted,
  output [7:0] Counter,
  output [1:0] Cycle
);

  wire and_1_out, and_2_out, and_3_out, clock_1_out, d_ff_1_qn, decoder_1_out0, decoder_1_out1,
       decoder_2_out0, demultiplexer_1_out0, demultiplexer_1_out1, multiplexer_1_out, not_1_out, not_2_out,
       not_3_out, not_4_out, or_1_out, t_ff_1_qn, xnor_1_out;
  wire [2:2] multiplexer_2_out;

  Multiplexer #(.select(1), .width(1)) multiplexer_1 (
    .in0(decoder_2_out0), .in1(Halt), .out(multiplexer_1_out), .sel(Halted));
  T_Flip_Flop #(.trigger("rising")) t_ff_1 (
    .clk(multiplexer_1_out), .T(1'b1), .Q(Halted), .Qn(t_ff_1_qn));  // open: preset, reset, en
  Clock #(.highDuration(1), .lowDuration(1)) clock_1 (.out(clock_1_out));
  and and_1 (and_1_out, clock_1_out, t_ff_1_qn);
  not not_1 (not_1_out, clock_1_out);
  and and_2 (and_2_out, decoder_2_out0, not_2_out);
  not not_2 (not_2_out, and_3_out);
  and and_3 (and_3_out, or_1_out, not_3_out);
  not not_3 (not_3_out, d_ff_1_qn);
  D_Flip_Flop #(.trigger("rising")) d_ff_1 (
    .clk(not_1_out), .D(and_2_out), .Qn(d_ff_1_qn));  // open: Q, preset, en, reset
  Demultiplexer #(.select(1), .width(1), .tristate("false")) demultiplexer_1 (
    .out0(demultiplexer_1_out0), .out1(demultiplexer_1_out1), .in(and_1_out), .sel(d_ff_1_qn));
  not not_4 (not_4_out, or_1_out);
  or or_1 (or_1_out, demultiplexer_1_out0, demultiplexer_1_out1);
  Counter #(.width(2), .max('h3), .ongoal("wrap"), .trigger("rising")) counter_1 (
    .Q(Cycle), .clk(demultiplexer_1_out1));  // open: load, D, count, carry, clr
  and and_4 (WCLK, not_4_out, decoder_1_out0);
  and and_5 (RCLK, not_4_out, decoder_1_out1);
  Decoder #(.select(1), .tristate("false")) decoder_1 (.out0(decoder_1_out0), .out1(decoder_1_out1), .sel(Cycle[0]));
  xnor xnor_1 (xnor_1_out, Cycle[0], Cycle[1]);
  Multiplexer #(.select(1), .width(4)) multiplexer_2 (
    .in0(Opcode), .in1(4'b0001), .out({fDec, multiplexer_2_out[2], selOperand}), .sel(xnor_1_out));
  Decoder #(.select(2), .tristate("false")) decoder_2 (
    .out0(decoder_2_out0), .sel(selOperand));  // open: out1, out2, out3
  // Probe on selOperand
  Counter #(.width(8), .max('hff), .ongoal("wrap"), .trigger("rising")) counter_2 (
    .Q(Counter), .clk(demultiplexer_1_out1));  // open: load, D, count, carry, clr
endmodule
